# Fritzing sketch ssd1306-oled-7pin-with-pico-w (saved by Fritzing 0.9.3b)
breadboards: 1

parts:
  Raspberry_Pico/Pico_W = Raspberry Pi Pico
  ssd1306_-_OLED_7_Pin_SPI = SPI OLED Monochrome 128x64 0.96 inch

nets:
  N1: Raspberry_Pico/Pico_W.pin_3, Raspberry_Pico/Pico_W.pin_8, Raspberry_Pico/Pico_W.pin_13, Raspberry_Pico/Pico_W.pin_18, Raspberry_Pico/Pico_W.pin_23, Raspberry_Pico/Pico_W.pin_28, Raspberry_Pico/Pico_W.pin_33, Raspberry_Pico/Pico_W.pin_38, ssd1306_-_OLED_7_Pin_SPI.GND
  N2: Raspberry_Pico/Pico_W.pin_21, ssd1306_-_OLED_7_Pin_SPI.CS
  N3: Raspberry_Pico/Pico_W.pin_22, ssd1306_-_OLED_7_Pin_SPI.DC
  N4: Raspberry_Pico/Pico_W.pin_24, ssd1306_-_OLED_7_Pin_SPI.SCK
  N5: Raspberry_Pico/Pico_W.pin_25, ssd1306_-_OLED_7_Pin_SPI.SDA
  N6: Raspberry_Pico/Pico_W.pin_26, ssd1306_-_OLED_7_Pin_SPI.RES
  N7: Raspberry_Pico/Pico_W.pin_36, ssd1306_-_OLED_7_Pin_SPI.VDD

notes:
  OLED PICO
  ----------------------------------------
  VCC 3.3(OUT) - 36
  GND GND - 38
  SCK/D0 GP18 - 24
  SDA/D1 GP19 - 25
  RES GP20 - 26
  DC GP17 - 22
  CS GP16 - 21

custom parts:
  Raspberry Pi Pico: Raspberry Pi Pico. Based around the RP2040 microcontroller the Pico is a low cost microcontroller device bringing Raspberry Pi quality, cost, and easy of use to the microcontroller space. Jan 2021, Split part in to two versions: SMD (this one) and tht. This one is single sided and uses the castellation pads to solder the module to the board (no holes, other than for the USB connector!). The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
  SPI OLED Monochrome 128x64 0.96 inch: Unknown 128x64 0.96 inch 128x64 SPI Monochrome OLED display
